// Logisim project 8_bit_CPU.circ as structural Verilog: 16 circuits, main circuit register_8_bit
module main (
  input  pc_rst,
  input  in_2,
  input  acc_rst,
  input  M_rst,
  input  [3:0] prog_addr,
  input  toggle_addr_mode,
  input  [7:0] prog_data,
  input  in_8,
  input  prog_bus_toggle,
  input  ram_rst,
  input  b_rst,
  input  ir_rst,
  input  in_13,
  input  c2_reset,
  input  [3:0] in_15
);

  wire A_L_U_cout, and_1_out, and_2_out, bcd_to_7_segment_decoder_2_p1, bcd_to_7_segment_decoder_3_p1,
       binary_to_bcd_converter_1_p2, clock_1_out, controlled_buffer_1_out, controlled_buffer_2_out, d_ff_1_q,
       d_ff_2_q, nor_1_out, nor_logic_1_out_2, not_1_out, not_2_out, not_3_out, or_1_out;
  wire [3:0] MAR_ram_out, multiplexer_2_out, multiplexer_3_out, PROGRAM_COUNTER_led;
  wire [5:0] zero_circuit_1_o;
  wire [7:0] Accumulator_alu_out, Accumulator_led, B_Register_alu_out, B_Register_led, IR_ledout,
       multiplexer_1_out, OUT_BUFFER_led, RAM_data_out, RAM_led, temp_reg_1_alu_out, temp_reg_1_led;
  wire [19:0] rom_1_data;

  and and_1 (and_1_out, zero_circuit_1_o[2], zero_circuit_1_o[3], zero_circuit_1_o[4], not_1_out);
  Clock clock_1 (.out(clock_1_out));
  not not_1 (not_1_out, zero_circuit_1_o[5]);
  LED led_1 (.in(not_2_out));
  counter_one MOD7_counter (.r2(and_1_out), .clk(not_2_out), .reset(c2_reset), .out_4(zero_circuit_1_o[5:2]));
  not not_2 (not_2_out, and_2_out);
  not not_3 (not_3_out, rom_1_data[5]);
  Hex_Digit_Display T (.value(zero_circuit_1_o[5:2]));  // open: dp
  DEC_416 DEC_4_to_16 (
    .a(zero_circuit_1_o[5]), .b(zero_circuit_1_o[4]), .c(zero_circuit_1_o[3]), .d(zero_circuit_1_o[2]));  // open: y9, ya, yb, yc, yd, ye, yf, y0, y1, y2, y3, y4, y5, y6, y7, y8
  and and_2 (and_2_out, clock_1_out, not_3_out);
  Multiplexer #(.width(8)) multiplexer_1 (
    .in0(RAM_data_out), .in1(prog_data), .out(multiplexer_1_out), .sel(prog_bus_toggle));
  or or_1 (or_1_out, prog_bus_toggle, rom_1_data[7]);
  nor nor_1 (nor_1_out, 1'b0, zero_circuit_1_o[3], zero_circuit_1_o[4], zero_circuit_1_o[5]);
  LED led_2 (.in(temp_reg_1_led[7]));
  LED led_3 (.in(temp_reg_1_led[6]));
  LED led_4 (.in(temp_reg_1_led[5]));
  Multiplexer #(.width(4)) multiplexer_2 (
    .in0(MAR_ram_out), .in1(prog_addr), .out(multiplexer_2_out), .sel(toggle_addr_mode));
  LED led_5 (.in(IR_ledout[7]));
  LED led_6 (.in(IR_ledout[6]));
  LED TT (.in(rom_1_data[0]));
  LED FI (.in(rom_1_data[4]));
  LED H (.in(rom_1_data[5]));
  LED led_7 (.in(temp_reg_1_led[4]));
  LED led_8 (.in(temp_reg_1_led[3]));
  LED led_9 (.in(temp_reg_1_led[2]));
  LED led_10 (.in(temp_reg_1_led[1]));
  mar_reg MAR (
    .Data_In(RAM_data_out[3:0]), .IE(rom_1_data[6]), .clock(and_2_out), .Reset(M_rst), .ram_Out(MAR_ram_out));  // open: LED
  RAM_16_Byte RAM (
    .wr(rom_1_data[8]), .addr(multiplexer_2_out), .data(multiplexer_1_out), .rd(or_1_out), .clock(and_2_out),
    .reset(ram_rst), .LED(RAM_led), .data_out(RAM_data_out));
  LED led_11 (.in(RAM_led[7]));
  LED led_12 (.in(RAM_led[6]));
  LED led_13 (.in(RAM_led[5]));
  LED led_14 (.in(IR_ledout[5]));
  LED led_15 (.in(IR_ledout[4]));
  LED led_16 (.in(IR_ledout[3]));
  LED led_17 (.in(IR_ledout[2]));
  LED MI (.in(rom_1_data[6]));
  LED RI (.in(rom_1_data[7]));
  LED RO (.in(rom_1_data[8]));
  temp_reg temp_reg_1 (
    .Data_In(RAM_data_out), .IE(rom_1_data[2]), .clock(and_2_out), .Reset(in_2), .OE(rom_1_data[1]),
    .ALU_OUT(temp_reg_1_alu_out), .LED(temp_reg_1_led), .Data_Out(RAM_data_out));
  LED led_18 (.in(temp_reg_1_led[0]));
  LED led_19 (.in(multiplexer_2_out[3]));
  LED led_20 (.in(multiplexer_2_out[2]));
  LED led_21 (.in(multiplexer_2_out[1]));
  LED led_22 (.in(multiplexer_2_out[0]));
  LED led_23 (.in(RAM_led[4]));
  LED led_24 (.in(RAM_led[3]));
  LED led_25 (.in(RAM_led[2]));
  LED led_26 (.in(RAM_led[1]));
  instruction_register IR (
    .OE(rom_1_data[9]), .re(ir_rst), .clk(and_2_out), .IE(rom_1_data[10]), .data_in(RAM_data_out),
    .lsb(RAM_data_out), .ledout(IR_ledout));  // open: msb
  LED led_27 (.in(IR_ledout[1]));
  LED led_28 (.in(IR_ledout[0]));
  LED IO (.in(rom_1_data[9]));
  LED II (.in(rom_1_data[10]));
  LED AI (.in(rom_1_data[11]));
  LED led_29 (.in(RAM_data_out[7]));
  LED led_30 (.in(RAM_data_out[6]));
  LED led_31 (.in(RAM_data_out[5]));
  LED led_32 (.in(RAM_data_out[4]));
  LED led_33 (.in(RAM_led[0]));
  Pull_Resistor pull_resistor_1 (.node(RAM_data_out[7]));
  Pull_Resistor pull_resistor_2 (.node(RAM_data_out[5]));
  Pull_Resistor pull_resistor_3 (.node(RAM_data_out[4]));
  Pull_Resistor pull_resistor_4 (.node(RAM_data_out[6]));
  Multiplexer #(.width(4)) multiplexer_3 (.in0(IR_ledout[7:4]), .in1(in_15), .out(multiplexer_3_out), .sel(nor_1_out));
  LED AO (.in(rom_1_data[12]));
  LED ALO (.in(rom_1_data[13]));
  LED led_34 (.in(RAM_data_out[3]));
  LED led_35 (.in(RAM_data_out[2]));
  LED led_36 (.in(RAM_data_out[1]));
  LED led_37 (.in(RAM_data_out[0]));
  Pull_Resistor pull_resistor_5 (.node(RAM_data_out[0]));
  Pull_Resistor pull_resistor_6 (.node(RAM_data_out[3]));
  Pull_Resistor pull_resistor_7 (.node(RAM_data_out[1]));
  Pull_Resistor pull_resistor_8 (.node(RAM_data_out[2]));
  Carry_circuit carry_circuit_1 (.op(IR_ledout[7:4]), .cin(d_ff_2_q), .o(zero_circuit_1_o[1]));
  LED SUB (.in(rom_1_data[14]));
  LED BI (.in(rom_1_data[15]));
  new_register OUT_BUFFER (
    .Data_In(RAM_data_out), .IE(rom_1_data[16]), .clock(and_2_out), .Reset(in_13), .LED(OUT_BUFFER_led));  // open: OE, ALU_OUT, Data_Out
  zero_circuit zero_circuit_1 (.op(IR_ledout[7:4]), .zin(d_ff_1_q), .o(zero_circuit_1_o[0]));
  LED ZE (.in(d_ff_1_q));
  LED CY (.in(d_ff_2_q));
  LED CE (.in(rom_1_data[17]));
  LED BuffIn (.in(rom_1_data[16]));
  parallel_load_counter PROGRAM_COUNTER (
    .out_enable(rom_1_data[18]), .clk(and_2_out), .load(rom_1_data[19]), .rst(pc_rst), .ce(rom_1_data[17]),
    .data_in(RAM_data_out[3:0]), .pc_out(RAM_data_out[3:0]), .led(PROGRAM_COUNTER_led));
  Hex_Digit_Display hex_digit_display_1 (.value(PROGRAM_COUNTER_led));  // open: dp
  ROM #(.addrWidth(10), .dataWidth(20)) rom_1 (.addr({multiplexer_3_out, zero_circuit_1_o}), .data(rom_1_data));
  LED CO (.in(rom_1_data[18]));
  LED JMP (.in(rom_1_data[19]));
  new_register Accumulator (
    .Data_In(RAM_data_out), .IE(rom_1_data[11]), .clock(and_2_out), .Reset(acc_rst), .OE(rom_1_data[12]),
    .ALU_OUT(Accumulator_alu_out), .LED(Accumulator_led), .Data_Out(RAM_data_out));
  ALU A_L_U (
    .B(B_Register_alu_out), .TMP(temp_reg_1_alu_out), .S_TMP(rom_1_data[0]), .A(Accumulator_alu_out),
    .SU(rom_1_data[14]), .OE(rom_1_data[13]), .alu_out(RAM_data_out), .cout(A_L_U_cout));
  Nor_logic nor_logic_1 (.in_1(RAM_data_out), .out_2(nor_logic_1_out_2));
  new_register B_Register (
    .Data_In(RAM_data_out), .IE(rom_1_data[15]), .clock(and_2_out), .Reset(b_rst), .OE(in_8),
    .ALU_OUT(B_Register_alu_out), .LED(B_Register_led), .Data_Out(RAM_data_out));
  _7_Segment_Display u_7_segment_display_1 ();  // open: g, f, a, b, e, d, c, dp
  _7_Segment_Display u_7_segment_display_2 ();  // open: g, f, a, b, e, d, c, dp
  // BCD_to_7_Segment_decoder bcd_to_7_segment_decoder_1: pin names not known
  // BCD_to_7_Segment_decoder bcd_to_7_segment_decoder_2: pin names not known; wires that end beside it: bcd_to_7_segment_decoder_2_p1
  // Binary_to_BCD_converter #(.binvalue(8)) binary_to_bcd_converter_1: pin names not known; wires that end beside it: OUT_BUFFER_led, binary_to_bcd_converter_1_p2, binary_to_bcd_converter_1_p2, bcd_to_7_segment_decoder_2_p1
  D_Flip_Flop d_ff_1 (
    .D(controlled_buffer_1_out), .clk(and_2_out), .Q(d_ff_1_q), .reset(rom_1_data[3]));  // open: Qn, preset
  assign controlled_buffer_1_out = rom_1_data[4] ? nor_logic_1_out_2 : 1'bz;  // Controlled_Buffer controlled_buffer_1
  _7_Segment_Display u_7_segment_display_3 ();  // open: g, f, a, b, e, d, c, dp
  // BCD_to_7_Segment_decoder bcd_to_7_segment_decoder_3: pin names not known; wires that end beside it: bcd_to_7_segment_decoder_3_p1, bcd_to_7_segment_decoder_3_p1
  LED led_38 (.in(Accumulator_led[7]));
  LED led_39 (.in(Accumulator_led[6]));
  LED led_40 (.in(Accumulator_led[5]));
  LED c (.in(A_L_U_cout));
  LED z (.in(nor_logic_1_out_2));
  LED led_41 (.in(d_ff_1_q));
  LED led_42 (.in(B_Register_led[7]));
  LED led_43 (.in(B_Register_led[6]));
  LED led_44 (.in(B_Register_led[5]));
  LED led_45 (.in(Accumulator_led[4]));
  LED led_46 (.in(Accumulator_led[3]));
  LED led_47 (.in(Accumulator_led[2]));
  LED led_48 (.in(Accumulator_led[1]));
  assign controlled_buffer_2_out = rom_1_data[4] ? A_L_U_cout : 1'bz;  // Controlled_Buffer controlled_buffer_2
  D_Flip_Flop d_ff_2 (
    .D(controlled_buffer_2_out), .clk(and_2_out), .Q(d_ff_2_q), .reset(rom_1_data[3]));  // open: Qn, preset
  LED led_49 ();  // open: in
  LED led_50 (.in(B_Register_led[4]));
  LED led_51 (.in(B_Register_led[3]));
  LED led_52 (.in(B_Register_led[2]));
  LED led_53 (.in(B_Register_led[1]));
  LED led_54 (.in(Accumulator_led[0]));
  LED led_55 (.in(B_Register_led[0]));

  // Notes on the sheet:
  //   T-
  //   7
  //   6
  //   5
  //   4
  //   3
  //   2
  //   1
  //   0
  //   contents of rom_1 (hex, n*v repeats v):
  //   40040 0 0 0 20500 67*0 240 0 0 0 900 59*0 240 0 0 0 8100 0 0 0 2810 55*0 a0200 65*0 a0200 0 0 0 8
  //   57*0 240 0 0 0 1080 59*0 204 0 0 0 2811 59*0 240 0 0 0 8100 0 0 0 6810 55*0 11000 64*0 a0200 0 0 0 8
  //   58*0 204 0 0 0 6811 59*0 20
  //   INSTRUCTION 
  //   DECODER
endmodule

module new_register (
  input  [7:0] Data_In,
  input  IE,
  input  OE,
  input  clock,
  input  Reset,
  output [7:0] ALU_OUT,
  output [7:0] LED,
  output [7:0] Data_Out
);

  Register register_1 (.D(Data_In), .en(IE), .clk(clock), .Q(ALU_OUT), .clr(Reset));
  assign Data_Out = OE ? ALU_OUT : 8'bz;  // Controlled_Buffer controlled_buffer_1

  assign LED = ALU_OUT;
endmodule

module ALU (
  input  [7:0] A,
  input  OE,
  input  [7:0] B,
  input  [7:0] TMP,
  input  S_TMP,
  input  SU,
  output [7:0] alu_out,
  output cout
);

  wire adder_1_cout, not_1_out;
  wire [7:0] adder_1_out, multiplexer_1_out, multiplexer_2_out, negator_1_out;

  Multiplexer #(.width(8)) multiplexer_1 (.in0(B), .in1(TMP), .out(multiplexer_1_out), .sel(S_TMP));
  Negator negator_1 (.in(multiplexer_1_out), .out(negator_1_out));
  Multiplexer #(.width(8)) multiplexer_2 (
    .in0(multiplexer_1_out), .in1(negator_1_out), .out(multiplexer_2_out), .sel(SU));
  Adder adder_1 (.a(A), .b(multiplexer_2_out), .out(adder_1_out), .cout(adder_1_cout));  // open: cin
  assign alu_out = OE ? adder_1_out : 8'bz;  // Controlled_Buffer controlled_buffer_1
  not not_1 (not_1_out, adder_1_cout);
  Multiplexer multiplexer_3 (.in0(adder_1_cout), .in1(not_1_out), .out(cout), .sel(SU));
endmodule

module register_8_bit (
  input  IE,
  input  I0,
  input  I1,
  input  I2,
  input  I3,
  input  I4,
  input  I5,
  input  I6,
  input  I7,
  input  OE,
  output L0,
  output O0,
  output L1,
  output O1,
  output L2,
  output O2,
  output L3,
  output O3,
  output L4,
  output O4,
  output L5,
  output O5,
  output L6,
  output O6,
  output L7,
  output O7
);

  wire and_1_out, and_2_out, and_3_out, and_4_out, and_5_out, and_6_out, and_7_out, and_8_out, and_9_out,
       and_10_out, and_11_out, and_12_out, and_13_out, and_14_out, and_15_out, and_16_out, clock_1_out,
       not_1_out, not_2_out, not_3_out, not_4_out, not_5_out, not_6_out, not_7_out, not_8_out, or_1_out,
       or_2_out, or_3_out, or_4_out, or_5_out, or_6_out, or_7_out, or_8_out;

  not not_1 (not_1_out, IE);
  not not_2 (not_2_out, IE);
  not not_3 (not_3_out, IE);
  not not_4 (not_4_out, IE);
  not not_5 (not_5_out, IE);
  not not_6 (not_6_out, IE);
  not not_7 (not_7_out, IE);
  not not_8 (not_8_out, IE);
  and and_1 (and_1_out, L0, not_1_out);
  and and_2 (and_2_out, IE, I0);
  and and_3 (and_3_out, L1, not_2_out);
  and and_4 (and_4_out, IE, I1);
  and and_5 (and_5_out, L2, not_3_out);
  and and_6 (and_6_out, IE, I2);
  and and_7 (and_7_out, L3, not_4_out);
  and and_8 (and_8_out, IE, I3);
  and and_9 (and_9_out, L4, not_5_out);
  and and_10 (and_10_out, IE, I4);
  and and_11 (and_11_out, L5, not_6_out);
  and and_12 (and_12_out, IE, I5);
  and and_13 (and_13_out, L6, not_7_out);
  and and_14 (and_14_out, IE, I6);
  and and_15 (and_15_out, L7, not_8_out);
  and and_16 (and_16_out, IE, I7);
  or or_1 (or_1_out, and_1_out, and_2_out);
  or or_2 (or_2_out, and_3_out, and_4_out);
  or or_3 (or_3_out, and_5_out, and_6_out);
  or or_4 (or_4_out, and_7_out, and_8_out);
  or or_5 (or_5_out, and_9_out, and_10_out);
  or or_6 (or_6_out, and_11_out, and_12_out);
  or or_7 (or_7_out, and_13_out, and_14_out);
  or or_8 (or_8_out, and_15_out, and_16_out);
  Clock clock_1 (.out(clock_1_out));
  D_Flip_Flop d_ff_1 (.D(or_1_out), .clk(clock_1_out), .Q(L0));  // open: Qn, preset, reset
  D_Flip_Flop d_ff_2 (.D(or_2_out), .clk(clock_1_out), .Q(L1));  // open: Qn, preset, reset
  D_Flip_Flop d_ff_3 (.D(or_3_out), .clk(clock_1_out), .Q(L2));  // open: Qn, preset, reset
  D_Flip_Flop d_ff_4 (.D(or_4_out), .clk(clock_1_out), .Q(L3));  // open: Qn, preset, reset
  D_Flip_Flop d_ff_5 (.D(or_5_out), .clk(clock_1_out), .Q(L4));  // open: Qn, preset, reset
  D_Flip_Flop d_ff_6 (.D(or_6_out), .clk(clock_1_out), .Q(L5));  // open: Qn, preset, reset
  D_Flip_Flop d_ff_7 (.D(or_7_out), .clk(clock_1_out), .Q(L6));  // open: Qn, preset, reset
  D_Flip_Flop d_ff_8 (.D(or_8_out), .clk(clock_1_out), .Q(L7));  // open: Qn, preset, reset
  assign O0 = OE ? L0 : 1'bz;  // Controlled_Buffer controlled_buffer_1
  assign O1 = OE ? L1 : 1'bz;  // Controlled_Buffer controlled_buffer_2
  assign O2 = OE ? L2 : 1'bz;  // Controlled_Buffer controlled_buffer_3
  assign O3 = OE ? L3 : 1'bz;  // Controlled_Buffer controlled_buffer_4
  assign O4 = OE ? L4 : 1'bz;  // Controlled_Buffer controlled_buffer_5
  assign O5 = OE ? L5 : 1'bz;  // Controlled_Buffer controlled_buffer_6
  assign O6 = OE ? L6 : 1'bz;  // Controlled_Buffer controlled_buffer_7
  assign O7 = OE ? L7 : 1'bz;  // Controlled_Buffer controlled_buffer_8

  // Notes on the sheet:
  //   this is a 8 bit register
endmodule

module RAM_16_Byte (
  input  rd,
  input  [3:0] addr,
  input  [7:0] data,
  input  wr,
  input  reset,
  input  clock,
  output [7:0] LED,
  output [7:0] data_out
);

  wire decoder_1_out0, decoder_1_out1, decoder_1_out2, decoder_1_out3, decoder_1_out4, decoder_1_out5,
       decoder_1_out6, decoder_1_out7, decoder_1_out8, decoder_1_out9, decoder_1_out10, decoder_1_out11,
       decoder_1_out12, decoder_1_out13, decoder_1_out14, decoder_1_out15;
  wire [7:0] demultiplexer_1_out0, demultiplexer_1_out1, demultiplexer_1_out2, demultiplexer_1_out3,
       demultiplexer_1_out4, demultiplexer_1_out5, demultiplexer_1_out6, demultiplexer_1_out7,
       demultiplexer_1_out8, demultiplexer_1_out9, demultiplexer_1_out10, demultiplexer_1_out11,
       demultiplexer_1_out12, demultiplexer_1_out13, demultiplexer_1_out14, demultiplexer_1_out15,
       register_1_q, register_2_q, register_3_q, register_4_q, register_5_q, register_6_q, register_7_q,
       register_8_q, register_9_q, register_10_q, register_11_q, register_12_q, register_13_q, register_14_q,
       register_15_q, register_16_q;

  Demultiplexer #(.select(4), .width(8)) demultiplexer_1 (
    .out0(demultiplexer_1_out0), .out1(demultiplexer_1_out1), .out2(demultiplexer_1_out2),
    .out3(demultiplexer_1_out3), .out4(demultiplexer_1_out4), .out5(demultiplexer_1_out5),
    .out6(demultiplexer_1_out6), .out7(demultiplexer_1_out7), .out8(demultiplexer_1_out8),
    .out9(demultiplexer_1_out9), .out10(demultiplexer_1_out10), .out11(demultiplexer_1_out11),
    .out12(demultiplexer_1_out12), .out13(demultiplexer_1_out13), .out14(demultiplexer_1_out14),
    .out15(demultiplexer_1_out15), .in(data), .sel(addr));
  Decoder #(.select(4)) decoder_1 (
    .out0(decoder_1_out0), .out1(decoder_1_out1), .out2(decoder_1_out2), .out3(decoder_1_out3),
    .out4(decoder_1_out4), .out5(decoder_1_out5), .out6(decoder_1_out6), .out7(decoder_1_out7),
    .out8(decoder_1_out8), .out9(decoder_1_out9), .out10(decoder_1_out10), .out11(decoder_1_out11),
    .out12(decoder_1_out12), .out13(decoder_1_out13), .out14(decoder_1_out14), .out15(decoder_1_out15),
    .sel(addr), .en(rd));
  Register register_1 (.D(demultiplexer_1_out0), .en(decoder_1_out0), .clk(clock), .Q(register_1_q), .clr(reset));
  Register register_2 (.D(demultiplexer_1_out1), .en(decoder_1_out1), .clk(clock), .Q(register_2_q), .clr(reset));
  Register register_3 (.D(demultiplexer_1_out2), .en(decoder_1_out2), .clk(clock), .Q(register_3_q), .clr(reset));
  Register register_4 (.D(demultiplexer_1_out3), .en(decoder_1_out3), .clk(clock), .Q(register_4_q), .clr(reset));
  Register register_5 (.D(demultiplexer_1_out4), .en(decoder_1_out4), .clk(clock), .Q(register_5_q), .clr(reset));
  Register register_6 (.D(demultiplexer_1_out5), .en(decoder_1_out5), .clk(clock), .Q(register_6_q), .clr(reset));
  Register register_7 (.D(demultiplexer_1_out6), .en(decoder_1_out6), .clk(clock), .Q(register_7_q), .clr(reset));
  Register register_8 (.D(demultiplexer_1_out7), .en(decoder_1_out7), .clk(clock), .Q(register_8_q), .clr(reset));
  Register register_9 (.D(demultiplexer_1_out8), .en(decoder_1_out8), .clk(clock), .Q(register_9_q), .clr(reset));
  Register register_10 (.D(demultiplexer_1_out9), .en(decoder_1_out9), .clk(clock), .Q(register_10_q), .clr(reset));
  Register register_11 (.D(demultiplexer_1_out10), .en(decoder_1_out10), .clk(clock), .Q(register_11_q), .clr(reset));
  Register register_12 (.D(demultiplexer_1_out11), .en(decoder_1_out11), .clk(clock), .Q(register_12_q), .clr(reset));
  Register register_13 (.D(demultiplexer_1_out12), .en(decoder_1_out12), .clk(clock), .Q(register_13_q), .clr(reset));
  Register register_14 (.D(demultiplexer_1_out13), .en(decoder_1_out13), .clk(clock), .Q(register_14_q), .clr(reset));
  Register register_15 (.D(demultiplexer_1_out14), .en(decoder_1_out14), .clk(clock), .Q(register_15_q), .clr(reset));
  Register register_16 (.D(demultiplexer_1_out15), .en(decoder_1_out15), .clk(clock), .Q(register_16_q), .clr(reset));
  Multiplexer #(.select(4), .width(8)) multiplexer_1 (
    .in0(register_1_q), .in1(register_2_q), .in2(register_3_q), .in3(register_4_q), .in4(register_5_q),
    .in5(register_6_q), .in6(register_7_q), .in7(register_8_q), .in8(register_9_q), .in9(register_10_q),
    .in10(register_11_q), .in11(register_12_q), .in12(register_13_q), .in13(register_14_q),
    .in14(register_15_q), .in15(register_16_q), .out(LED), .sel(addr));
  assign data_out = wr ? LED : 8'bz;  // Controlled_Buffer controlled_buffer_1
endmodule

module mar_reg (
  input  [3:0] Data_In,
  input  IE,
  input  clock,
  input  Reset,
  output [3:0] LED,
  output [3:0] ram_Out
);

  Register #(.width(4)) register_1 (.D(Data_In), .en(IE), .clk(clock), .Q(LED), .clr(Reset));

  assign ram_Out = LED;
endmodule

module program_counter (
  input  jmp,
  input  in_2,
  input  CE,
  input  clk,
  input  reset,
  input  OE,
  output [3:0] led,
  output [3:0] Cout
);

  wire and_1_out, and_2_out, controlled_buffer_2_out, controlled_buffer_3_out, controlled_buffer_4_out,
       controlled_buffer_6_out, not_1_out;

  Controlled_Buffer #(.width(4)) controlled_buffer_1 (.en(jmp));  // open: in, out
  not not_1 (not_1_out, in_2);
  assign controlled_buffer_2_out = CE ? CE : 1'bz;  // Controlled_Buffer controlled_buffer_2
  J_K_Flip_Flop j_k_ff_1 (
    .J(controlled_buffer_2_out), .K(controlled_buffer_2_out), .clk(clk), .Q(led[0]), .reset(reset));  // open: Qn, preset
  assign controlled_buffer_3_out = CE ? led[0] : 1'bz;  // Controlled_Buffer controlled_buffer_3
  J_K_Flip_Flop j_k_ff_2 (
    .J(controlled_buffer_3_out), .K(controlled_buffer_3_out), .clk(clk), .Q(led[1]), .reset(reset));  // open: Qn, preset
  assign controlled_buffer_4_out = CE ? led[1] : 1'bz;  // Controlled_Buffer controlled_buffer_4
  and and_1 (and_1_out, led[0], led[1]);
  J_K_Flip_Flop j_k_ff_3 (
    .J(and_1_out), .K(controlled_buffer_4_out), .clk(clk), .Q(led[2]), .reset(reset));  // open: Qn, preset
  Hex_Digit_Display hex_digit_display_1 (.value(led));  // open: dp
  assign Cout = OE ? led : 4'bz;  // Controlled_Buffer controlled_buffer_5
  and and_2 (and_2_out, led[0], led[1], led[2]);
  assign controlled_buffer_6_out = CE ? and_2_out : 1'bz;  // Controlled_Buffer controlled_buffer_6
  J_K_Flip_Flop j_k_ff_4 (
    .J(and_2_out), .K(controlled_buffer_6_out), .clk(clk), .Q(led[3]), .reset(reset));  // open: Qn, preset

  // Notes on the sheet:
  //   d
  //   c
  //   b
  //   a
endmodule

module instruction_register (
  input  OE,
  input  [7:0] data_in,
  input  IE,
  input  re,
  input  clk,
  output [7:0] lsb,
  output [7:0] msb,
  output [7:0] ledout
);

  Register register_1 (.D(data_in), .en(IE), .clk(clk), .Q(ledout), .clr(re));
  assign lsb = OE ? {4'b0000, ledout[3:0]} : 8'bz;  // Controlled_Buffer controlled_buffer_1

  assign msb = {ledout[7:4], 4'b0000};
endmodule

module counter_one (
  input  reset,
  input  r2,
  input  clk,
  output [3:0] out_4
);

  wire or_1_out;

  or or_1 (or_1_out, reset, r2);
  J_K_Flip_Flop #(.trigger("falling")) j_k_ff_1 (
    .J(1'b1), .K(1'b1), .clk(clk), .Q(out_4[0]), .reset(or_1_out));  // open: Qn, preset
  J_K_Flip_Flop #(.trigger("falling")) j_k_ff_2 (
    .J(1'b1), .K(1'b1), .clk(out_4[0]), .Q(out_4[1]), .reset(or_1_out));  // open: Qn, preset
  J_K_Flip_Flop #(.trigger("falling")) j_k_ff_3 (
    .J(1'b1), .K(1'b1), .clk(out_4[1]), .Q(out_4[2]), .reset(or_1_out));  // open: Qn, preset
  J_K_Flip_Flop #(.trigger("falling")) j_k_ff_4 (
    .J(1'b1), .K(1'b1), .clk(out_4[2]), .Q(out_4[3]), .reset(or_1_out));  // open: Qn, preset
endmodule

module DEC_416 (
  input  a,
  input  b,
  input  c,
  input  d,
  output y0,
  output y1,
  output y2,
  output y3,
  output y4,
  output y5,
  output y6,
  output y7,
  output y8,
  output y9,
  output ya,
  output yb,
  output yc,
  output yd,
  output ye,
  output yf
);

  wire not_1_out, not_2_out, not_3_out, not_4_out;

  not not_1 (not_1_out, a);
  not not_2 (not_2_out, b);
  not not_3 (not_3_out, c);
  not not_4 (not_4_out, d);
  and and_1 (y0, not_4_out, not_3_out, not_2_out, not_1_out);
  and and_2 (y1, d, not_3_out, not_2_out, not_1_out);
  and and_3 (y2, not_4_out, c, not_2_out, not_1_out);
  and and_4 (y3, d, c, not_2_out, not_1_out);
  and and_5 (y4, not_4_out, not_3_out, b, not_1_out);
  and and_6 (y5, d, not_3_out, b, not_1_out);
  and and_7 (y6, not_4_out, c, b, not_1_out);
  and and_8 (y7, d, c, b, not_1_out);
  and and_9 (y8, not_4_out, not_3_out, not_2_out, a);
  and and_10 (y9, d, not_3_out, not_2_out, a);
  and and_11 (ya, not_4_out, c, not_2_out, a);
  and and_12 (yb, d, c, not_2_out, a);
  and and_13 (yc, not_4_out, not_3_out, b, a);
  and and_14 (yd, d, not_3_out, b, a);
  and and_15 (ye, not_4_out, c, b, a);
  and and_16 (yf, a, b, c, d);
endmodule

module FlagReg (
  input  rst,
  input  IE,
  input  clk,
  input  c,
  input  z,
  output cf,
  output zf,
  output out_8,
  output out_9,
  output out_10,
  output out_11,
  output out_12,
  output out_13
);

  // Shift_Register shift_register_1: pin names not known; wires that end beside it: rst, IE, clk, c, z, cf, zf, out_8, out_9, out_10, out_11, out_12, out_13
endmodule

module Nor_logic (
  input  [7:0] in_1,
  output out_2
);

  nor nor_1 (out_2, in_1[0], in_1[1], in_1[2], in_1[3], in_1[4], in_1[5], in_1[6], in_1[7]);
endmodule

module parallel_load_counter (
  input  [3:0] data_in,
  input  load,
  input  clk,
  input  rst,
  input  ce,
  input  out_enable,
  output [3:0] led,
  output [3:0] pc_out
);

  wire controlled_buffer_1_out, multiplexer_1_out, multiplexer_2_out, multiplexer_3_out, multiplexer_4_out,
       multiplexer_5_out, multiplexer_6_out, multiplexer_7_out, not_1_out, not_2_out, not_3_out, not_4_out,
       not_5_out, not_6_out, not_7_out, not_8_out, not_9_out, not_10_out, or_1_out, or_2_out, or_3_out,
       or_4_out;

  not not_1 (not_1_out, clk);
  assign controlled_buffer_1_out = ce ? not_1_out : 1'bz;  // Controlled_Buffer controlled_buffer_1
  not not_2 (not_2_out, load);
  not not_3 (not_3_out, load);
  or or_1 (or_1_out, not_3_out, not_4_out);
  Multiplexer multiplexer_1 (.in0(not_2_out), .in1(data_in[0]), .out(multiplexer_1_out), .sel(load));
  not not_4 (not_4_out, multiplexer_1_out);
  J_K_Flip_Flop #(.trigger("falling")) j_k_ff_1 (
    .J(multiplexer_1_out), .K(or_1_out), .clk(controlled_buffer_1_out), .Q(led[0]), .reset(rst));  // open: Qn, preset
  not not_5 (not_5_out, load);
  Multiplexer multiplexer_2 (.in0(not_2_out), .in1(data_in[1]), .out(multiplexer_2_out), .sel(load));
  not not_6 (not_6_out, multiplexer_2_out);
  or or_2 (or_2_out, not_5_out, not_6_out);
  Multiplexer multiplexer_3 (.in0(led[0]), .in1(controlled_buffer_1_out), .out(multiplexer_3_out), .sel(load));
  J_K_Flip_Flop #(.trigger("falling")) j_k_ff_2 (
    .J(multiplexer_2_out), .K(or_2_out), .clk(multiplexer_3_out), .Q(led[1]), .reset(rst));  // open: Qn, preset
  Multiplexer multiplexer_4 (.in0(not_2_out), .in1(data_in[2]), .out(multiplexer_4_out), .sel(load));
  not not_7 (not_7_out, load);
  or or_3 (or_3_out, not_7_out, not_8_out);
  Multiplexer multiplexer_5 (.in0(led[1]), .in1(controlled_buffer_1_out), .out(multiplexer_5_out), .sel(load));
  not not_8 (not_8_out, multiplexer_4_out);
  J_K_Flip_Flop #(.trigger("falling")) j_k_ff_3 (
    .J(multiplexer_4_out), .K(or_3_out), .clk(multiplexer_5_out), .Q(led[2]), .reset(rst));  // open: Qn, preset
  assign pc_out = out_enable ? led : 4'bz;  // Controlled_Buffer controlled_buffer_2
  not not_9 (not_9_out, load);
  or or_4 (or_4_out, not_9_out, not_10_out);
  Multiplexer multiplexer_6 (.in0(not_2_out), .in1(data_in[3]), .out(multiplexer_6_out), .sel(load));
  not not_10 (not_10_out, multiplexer_6_out);
  Multiplexer multiplexer_7 (.in0(led[2]), .in1(controlled_buffer_1_out), .out(multiplexer_7_out), .sel(load));
  J_K_Flip_Flop #(.trigger("falling")) j_k_ff_4 (
    .J(multiplexer_6_out), .K(or_4_out), .clk(multiplexer_7_out), .Q(led[3]), .reset(rst));  // open: Qn, preset
endmodule

module Carry_circuit (
  input  cin,
  input  [3:0] op,
  output o
);

  wire not_1_out, not_2_out, not_3_out;

  not not_1 (not_1_out, op[3]);
  not not_2 (not_2_out, op[1]);
  not not_3 (not_3_out, op[0]);
  and and_1 (o, not_1_out, op[2], not_2_out, not_3_out, cin);
endmodule

module temp_reg (
  input  [7:0] Data_In,
  input  IE,
  input  OE,
  input  clock,
  input  Reset,
  output [7:0] ALU_OUT,
  output [7:0] LED,
  output [7:0] Data_Out
);

  Register register_1 (.D(Data_In), .en(IE), .clk(clock), .Q(ALU_OUT), .clr(Reset));
  assign Data_Out = OE ? ALU_OUT : 8'bz;  // Controlled_Buffer controlled_buffer_1

  assign LED = ALU_OUT;
endmodule

module zero_circuit (
  input  zin,
  input  [3:0] op,
  output o
);

  wire not_1_out, not_2_out;

  not not_1 (not_1_out, op[2]);
  not not_2 (not_2_out, op[1]);
  and and_1 (o, op[3], not_1_out, not_2_out, op[0], zin);
endmodule
